# Fritzing sketch Leeroy (saved by Fritzing 0.7.5b)
breadboards: 1

parts:
  LED2 = LED - 5mm [color="Red (633nm)" package="5 mm [THT]"]
  LED1 = LED - 5mm [color="Green (555nm)" package="5 mm [THT]"]
  Arduino1 = Arduino
  R1 = Resistor [tolerance=±5% resistance=220 package=THT]
  R2 = Resistor [tolerance=±5% resistance=220 package=THT]

nets:
  N1: LED2.cathode, Arduino1.D4
  N2: LED2.anode, R1.Pin_0
  N3: LED1.cathode, Arduino1.D2
  N4: LED1.anode, R2.Pin_0
  N5: Arduino1.GND, R1.Pin_1, R2.Pin_1

notes:
  Etheret PRO really but any arduino and a Ethernet Shield will do
